# Fritzing sketch OpenOceanBuddyLocator (saved by Fritzing 0.9.3b)

parts:
  M1 = Sony Spresense
  Part1 = 16 NeoPixel Ring [part_number=1463]
  Part2 = Adafruit LSM303DLHC Triple-axis Accelerometer+Magnetometer (Compass) [part_number="Adafruit #1120"]
  Part3 = Arduino Nano (Rev3.0)
  Part4 = NRF24L01+ Breakout Board
  YL-1 = YL-105 [part_number=YL-105]
  M2 = RioRand LM2596
  U1 = LIPO-1000mAh [package=lipo-1000]
  Grove1 = Grove OLED 128x96
  TP1 = TP4056 [chip_label=TP4056 package="DIP (Dual Inline) [THT]"]
  Part6 = Logic Level Converter
  Part7 = Logic Level Converter
  C4 = Ceramic Capacitor [capacitance=1µF voltage=16V package="0805 [SMD, multilayer]"]  # not connected
  C5 = Ceramic Capacitor [capacitance=100nF voltage=16V package="0805 [SMD, multilayer]"]
  C3 = Electrolytic Capacitor [capacitance=10µF voltage=16V package="0405 [SMD, electrolytic]"]
  C1 = Electrolytic Capacitor [capacitance=100µF voltage=16V package="200 mil [THT, electrolytic]"]
  C2 = Electrolytic Capacitor [capacitance=100µF voltage=16V package="200 mil [THT, electrolytic]"]
  R1 = Resistor [tolerance=±1% resistance=62k package=THT]
  R2 = Resistor [tolerance=±1% resistance=10k package=THT]

nets:
  GND: M1.GND, M1.D25, Part1.GND, Part2.GND, Part3.GND, YL-1.GND, M2.Pin_4, Grove1.GND, Part6.GND, Part7.GND, C1.-
  N1: M1.D01, Part7.RX_LV
  N2: M1.D23, Part6.RX2_LV
  N3: M1.1.8V, Part6.LV, Part7.LV
  N4: M1.A3, R1.Pin_0, R2.Pin_0
  N5: M1.D14, Part7.TX2_LV
  N6: M1.D15, Part7.RX2_LV
  N7: M1.D16, Part7.TX_LV
  N8: M1.D17, Part6.TX2_LV
  N9: M1.D18, Part6.RX_LV
  N10: M1.D19, Part6.TX_LV
  N11: Part1.IN, Part3.D6
  VIN: Part1.VDD, Part2.VIN, Part3.VIN, YL-1.VCC, M2.Pin_3, Grove1.VCC, Part6.HV, Part7.HV, C1.+
  N12: Part2.SCL, Part3.A5
  N13: Part2.SDA, Part3.A4
  N14: Part3.D2, Part7.RX_HV
  N15: Part4.CE, Part6.TX_HV
  N16: Part4.CS, Part6.RX_HV
  N17: Part4.SCK, Part6.RX2_HV
  N18: Part4.MOSI, Part7.TX_HV
  N19: Part4.MISO, Part6.TX2_HV
  N20: M2.Pin_1, TP1.pin3
  N21: M2.Pin_2, TP1.pin6
  N22: U1.+, TP1.pin4, R1.Pin_1
  N23: U1.-, TP1.pin5, R2.Pin_1
  N24: Grove1.SDA, Part7.TX2_HV
  N25: Grove1.SCL, Part7.RX2_HV
  N26: C5.0, C2.-
  N27: C5.1, C3.-, C2.+

notes:
  Battery connects to the + terminal CN1
  The charger (TP1) board is there just for LiPo protection if your battery doesn't have one.
  Pin D25 to GND for second module only (cyan wire)

custom parts:
  Sony Spresense: Sony CXD 5602 PWBMAIN 1 ARM® Cortex®-M4F x 6 cores Flash memory 8 MB, SRAM 8 MB Maximum clock frequency 156 MHz, Digital input / output GPIO, SPI, I2C, UART, I2S, GPS, GLONASS
  16 NeoPixel Ring: 16 ultra bright smart LED NeoPixels are arranged in a circle with 1.75" (44.5mm) outer diameter. The rings are 'chainable' - connect the output pin of one to the input pin of another. Use only one microcontroller pin to control as many as you can chain together! Each LED is addressable as the driver chip is inside the LED. Each one has ~18mA constant current drive so the color will be very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
  Adafruit LSM303DLHC Triple-axis Accelerometer+Magnetometer (Compass): He told you "Go West, young maker!" - but you don't know which way is West! Ah, if only you had this triple-axis accelerometer/magnetometer compass module. Inside are two sensors, one is a classic 3-axis accelerometer, which can tell you which direction is down towards the Earth (by measuring gravity). The other is a magnetometer that can sense where the strongest magnetic force is coming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
  TP4056: A DIP stand-in part for whatever IC you want. With 6 pins on a 300mil dual inline package (DIP) footprint.
